# Fritzing sketch SmartCoil_sketch (saved by Fritzing 0.9.3b)

parts:
  proto1 = Adafruit_PermaProto_1_4_Board
  Raspberry_Pi_1 = Raspberry Pi 3 [part_number=RPI-3-V1.2]
  Part1 = Adafruit BME680
  U1 = 4-Channel 5v Relay Shield [package=relay-4ch5v10a]
  U2 = Mystery Part - 5 pins [chip_label="Fan Coil Unit (wall)" package=THT]
  LED1 = smd LED [color="Blue (430nm)" package="1206 [SMD]"]  # not connected
  R1 = Resistor [tolerance=±5% resistance=1k package="2512 [SMD]"]  # not connected

nets:
  N1: proto1.connectorA2, Part1.SDI/SDA
  N2: proto1.connectorA3, Part1.SCK/SCL
  N3: proto1.connectorA6, U1.IN1
  N4: proto1.connectorB6, proto1.connectorC14
  N5: proto1.connectorB8, U1.IN2
  N6: proto1.connectorC7, U1.IN4
  N7: proto1.connectorE2, Raspberry_Pi_1.GPIO2
  N8: proto1.connectorE3, Raspberry_Pi_1.GPIO3
  N9: proto1.connectorE6, Raspberry_Pi_1.GPIO17
  N10: proto1.connectorE7, Raspberry_Pi_1.GPIO27
  N11: proto1.connectorE8, Raspberry_Pi_1.GPIO22
  N12: proto1.connectorF8, Raspberry_Pi_1.GPIO23
  N13: proto1.connectorH8, U1.IN3
  3V3: proto1.connectorW1, proto1.connectorZ1, Raspberry_Pi_1.3v3, Raspberry_Pi_1.3V3
  N14: proto1.connectorW15, Part1.VIN
  N15: proto1.connectorX1, Raspberry_Pi_1.GND
  N16: proto1.connectorX14, Part1.GND
  N17: proto1.connectorY1, Raspberry_Pi_1.5V
  N18: proto1.connectorY14, U1.VCC
  N19: proto1.connectorZ8, U1.GND
  N20: U1.K1-Off, U1.K2-Off, U1.K3-Off, U1.K4-Off, U2.positive
  N21: U1.K1-On, U2.water_valve
  N22: U1.K2-On, U2.fan_lo_speed
  N23: U1.K3-On, U2.fan_mi_speed
  N24: U1.K4-On, U2.fan_hi_speed

notes:
  Fan Coil Unit (wall)
  water   fan low   fan mid   fan high
  valve    speed      speed      speed
  110V

custom parts:
  4-Channel 5v Relay Shield: 4 Channel 5v Relay Shield w. 2x SPD-06VDC-SD-C
  Mystery Part - 5 pins: A dummy, proxy, ersatz, stand-in part for whatever you want. With 5 pins on a 100 mil inline pin header footprint.
